// Logisim project ENCODER.circ as structural Verilog: 9 circuits, main circuit main
module main (
  input  P15,
  input  P14,
  input  P13,
  input  P12,
  input  P11,
  input  P10,
  input  P9,
  input  P8,
  input  P7,
  input  P6,
  input  P5,
  input  P4,
  input  P3,
  input  P2,
  input  BUSSES,
  input  TRUCKS,
  input  _4WHEELER,
  input  _2WHEELER,
  input  P1,
  input  P0,
  output out_21,
  output out_22,
  output out_23,
  output out_24
);

  wire and_1_out, and_2_out, and_3_out, and_4_out, and_5_out, and_6_out, and_7_out, and_8_out, and_11_out,
       not_1_out, not_2_out, not_3_out, not_4_out, not_5_out, pe1_2_out_5, pe1_2_out_6, PE1_out_5, PE1_out_6,
       PE2_out_5, PE2_out_6, PE3_out_5, PE3_out_6, PE4_out_5, PE4_out_6;

  PE4 PE4 (.D15(P15), .D14(P14), .D13(P13), .D12(P12), .out_5(PE4_out_5), .out_6(PE4_out_6));
  PE3 PE3 (.D12(P11), .D11(P10), .D10(P9), .D9(P8), .out_5(PE3_out_5), .out_6(PE3_out_6));
  PE2 PE2 (.D7(P7), .D6(P6), .D5(P5), .D4(P4), .out_5(PE2_out_5), .out_6(PE2_out_6));
  PE1 PE1 (.D3(P3), .D2(P2), .D1(P1), .D0(P0), .out_5(PE1_out_5), .out_6(PE1_out_6));
  and and_1 (and_1_out, PE4_out_5, BUSSES);
  and and_2 (and_2_out, PE3_out_5, TRUCKS);
  and and_3 (and_3_out, PE2_out_5, _4WHEELER);
  and and_4 (and_4_out, PE4_out_6, BUSSES);
  and and_5 (and_5_out, PE3_out_6, TRUCKS);
  and and_6 (and_6_out, PE2_out_6, _4WHEELER);
  and and_7 (and_7_out, PE1_out_5, _2WHEELER);
  and and_8 (and_8_out, PE1_out_6, _2WHEELER);
  or or_1 (out_24, and_4_out, and_5_out, and_6_out, and_8_out);
  and and_9 (out_21, pe1_2_out_5, not_5_out);
  and and_10 (out_22, pe1_2_out_6, not_5_out);
  PE1 pe1_2 (.D3(BUSSES), .D2(TRUCKS), .D1(_4WHEELER), .D0(_2WHEELER), .out_5(pe1_2_out_5), .out_6(pe1_2_out_6));
  not not_1 (not_1_out, BUSSES);
  not not_2 (not_2_out, TRUCKS);
  not not_3 (not_3_out, _4WHEELER);
  not not_4 (not_4_out, _2WHEELER);
  or or_2 (out_23, and_1_out, and_7_out, and_2_out, and_3_out);
  not not_5 (not_5_out, and_11_out);
  and and_11 (and_11_out, not_1_out, not_2_out, not_3_out, not_4_out);
  LED led_1 (.in(not_5_out));
  LED led_2 (.in(and_11_out));

  // Notes on the sheet:
  //   BUSSES
  //   TRUCKS
  //   4WHEELERS
  //   2WHEELERS
  //   ON INPUT PARKING SYMBOLIZES VACANCY
  //   _____________________________
  //   ____________________________
  //   ____________________________
  //   VACANT PARKING SLOT DETECTOR
  //   APPROPRIATE VACANT PARKING SLOT DISPLAY (IN BINARY)
  //   SYSTEM ACTIVATE
  //   SYSTEM DEACTIVATE
endmodule

module PE1 (
  input  D3,
  input  D2,
  input  D1,
  input  D0,
  output out_5,
  output out_6
);

  wire and_1_out, and_2_out, not_1_out, not_2_out, not_3_out;

  not not_1 (not_1_out, D2);
  not not_2 (not_2_out, D1);
  not not_3 (not_3_out, D0);
  and and_1 (and_1_out, not_1_out, not_3_out);
  and and_2 (and_2_out, D1, not_3_out);
  and and_3 (out_5, not_2_out, not_3_out);
  or or_1 (out_6, and_1_out, and_2_out);
endmodule

module PE2 (
  input  D7,
  input  D6,
  input  D5,
  input  D4,
  output out_5,
  output out_6
);

  wire and_1_out, and_2_out, not_1_out, not_2_out, not_3_out;

  not not_1 (not_1_out, D6);
  not not_2 (not_2_out, D5);
  not not_3 (not_3_out, D4);
  and and_1 (and_1_out, not_1_out, not_3_out);
  and and_2 (and_2_out, D5, not_3_out);
  and and_3 (out_5, not_2_out, not_3_out);
  or or_1 (out_6, and_1_out, and_2_out);
endmodule

module PE3 (
  input  D12,
  input  D11,
  input  D10,
  input  D9,
  output out_5,
  output out_6
);

  wire and_1_out, and_2_out, not_1_out, not_2_out, not_3_out;

  not not_1 (not_1_out, D11);
  not not_2 (not_2_out, D10);
  not not_3 (not_3_out, D9);
  and and_1 (and_1_out, not_1_out, not_3_out);
  and and_2 (and_2_out, D10, not_3_out);
  and and_3 (out_5, not_2_out, not_3_out);
  or or_1 (out_6, and_1_out, and_2_out);
endmodule

module PE4 (
  input  D15,
  input  D14,
  input  D13,
  input  D12,
  output out_5,
  output out_6
);

  wire and_1_out, and_2_out, not_1_out, not_2_out, not_3_out;

  not not_1 (not_1_out, D14);
  not not_2 (not_2_out, D13);
  not not_3 (not_3_out, D12);
  and and_1 (and_1_out, not_1_out, not_3_out);
  and and_2 (and_2_out, D13, not_3_out);
  and and_3 (out_5, not_2_out, not_3_out);
  or or_1 (out_6, and_1_out, and_2_out);
endmodule

module Password_Input (
  input  in_1,
  input  in_2,
  input  in_3,
  input  LSB,
  input  Enter_Button,
  output BUSSES,
  output TRUCKS,
  output _4WHEELER,
  output _2WHEELER
);

  wire not_1_out, not_2_out, not_3_out, not_4_out;

  not not_1 (not_1_out, in_1);
  not not_2 (not_2_out, in_2);
  not not_3 (not_3_out, in_3);
  not not_4 (not_4_out, LSB);
  and and_1 (BUSSES, Enter_Button, not_3_out, not_2_out, in_1);
  and and_2 (TRUCKS, not_4_out, not_3_out, not_1_out, in_2, Enter_Button);
  and and_3 (_4WHEELER, Enter_Button, not_1_out, not_4_out, in_3, not_2_out);
  and and_4 (_2WHEELER, Enter_Button, not_1_out, not_2_out, not_3_out, LSB);

  // Notes on the sheet:
  //   VEHICLE TYPE KEYCODE INPUT
  //   PASSWORDS
  //   4WHEELER: 0010
  //   TRUCKS: 0100
  //   BUSSES: 1000
  //   2WHEELER : 0001
endmodule

module Password_Trials (
  input  PASSWORD_INPUT,
  input  in_2,
  input  in_3,
  input  LSB,
  output _2WHEELER,
  output _4WHEELER,
  output TRUCKS,
  output BUSSES
);

  wire and_1_out, button_1_out, not_1_out, password_input_1__2wheeler, password_input_1__4wheeler,
       password_input_1_busses, password_input_1_trucks, t_ff_1_q, t_ff_2_q;

  Button button_1 (.out(button_1_out));
  Password_Input password_input_1 (
    .in_1(PASSWORD_INPUT), .in_2(in_2), .in_3(in_3), .LSB(LSB), .Enter_Button(button_1_out),
    .BUSSES(password_input_1_busses), .TRUCKS(password_input_1_trucks),
    ._4WHEELER(password_input_1__4wheeler), ._2WHEELER(password_input_1__2wheeler));
  T_Flip_Flop t_ff_1 (.clk(button_1_out), .T(1'b1), .Q(t_ff_1_q));  // open: Qn, preset, reset, en
  and and_1 (and_1_out, t_ff_2_q, t_ff_1_q);
  not not_1 (not_1_out, and_1_out);
  T_Flip_Flop t_ff_2 (.clk(button_1_out), .T(t_ff_1_q), .Q(t_ff_2_q));  // open: Qn, preset, reset, en
  and and_2 (_2WHEELER, password_input_1__2wheeler, not_1_out);
  LED led_1 (.in(and_1_out));
  and and_3 (_4WHEELER, password_input_1__4wheeler, not_1_out);
  and and_4 (TRUCKS, password_input_1_trucks, not_1_out);
  and and_5 (BUSSES, password_input_1_busses, not_1_out);

  // Notes on the sheet:
  //   Press to Enter Password
  //   PASSWORD TRIALS INPUT SECTION
  //   VALIDATE ONLY ONCE TRIALS IS LESS THAN 3 (NOT 3)
  //   Disable System, excess incorrect trials
endmodule

module Main (
  input  P15,
  input  P14,
  input  P13,
  input  P12,
  input  P11,
  input  P10,
  input  P9,
  input  P8,
  input  P7,
  input  P6,
  input  P5,
  input  P4,
  input  P3,
  input  P2,
  input  P1,
  input  P0,
  output out_17,
  output out_18,
  output out_19,
  output out_20
);

  wire and_1_out, and_2_out, and_3_out, and_4_out, and_5_out, and_6_out, and_7_out, and_8_out, and_11_out,
       clock_1_out, not_1_out, not_2_out, not_3_out, not_4_out, not_5_out, pe1_2_out_5, pe1_2_out_6,
       PE1_out_5, PE1_out_6, PE2_out_5, PE2_out_6, PE3_out_5, PE3_out_6, PE4_out_5, PE4_out_6,
       random_2power_gen_1_out_2, random_2power_gen_1_out_3, random_2power_gen_1_out_4,
       random_2power_gen_1_out_5;

  LED led_1 ();  // open: in
  LED led_2 ();  // open: in
  LED led_3 ();  // open: in
  LED led_4 ();  // open: in
  LED led_5 ();  // open: in
  LED led_6 ();  // open: in
  LED led_7 ();  // open: in
  LED led_8 ();  // open: in
  LED led_9 ();  // open: in
  LED led_10 ();  // open: in
  LED led_11 ();  // open: in
  LED led_12 ();  // open: in
  LED led_13 ();  // open: in
  LED led_14 ();  // open: in
  LED led_15 ();  // open: in
  LED led_16 ();  // open: in
  Clock #(.highDuration(3)) clock_1 (.out(clock_1_out));
  PE4 PE4 (.D15(P15), .D14(P14), .D13(P13), .D12(P12), .out_5(PE4_out_5), .out_6(PE4_out_6));
  PE3 PE3 (.D12(P11), .D11(P10), .D10(P9), .D9(P8), .out_5(PE3_out_5), .out_6(PE3_out_6));
  PE2 PE2 (.D7(P7), .D6(P6), .D5(P5), .D4(P4), .out_5(PE2_out_5), .out_6(PE2_out_6));
  PE1 PE1 (.D3(P3), .D2(P2), .D1(P1), .D0(P0), .out_5(PE1_out_5), .out_6(PE1_out_6));
  Random_2Power_Gen random_2power_gen_1 (
    .in_1(clock_1_out), .out_2(random_2power_gen_1_out_2), .out_3(random_2power_gen_1_out_3),
    .out_4(random_2power_gen_1_out_4), .out_5(random_2power_gen_1_out_5));
  and and_1 (and_1_out, PE4_out_5, random_2power_gen_1_out_2);
  and and_2 (and_2_out, PE4_out_6, random_2power_gen_1_out_2);
  and and_3 (and_3_out, PE3_out_5, random_2power_gen_1_out_3);
  and and_4 (and_4_out, PE2_out_5, random_2power_gen_1_out_4);
  and and_5 (and_5_out, PE3_out_6, random_2power_gen_1_out_3);
  and and_6 (and_6_out, PE2_out_6, random_2power_gen_1_out_4);
  and and_7 (and_7_out, PE1_out_5, random_2power_gen_1_out_5);
  and and_8 (and_8_out, PE1_out_6, random_2power_gen_1_out_5);
  or or_1 (out_20, and_2_out, and_5_out, and_6_out, and_8_out);
  and and_9 (out_17, pe1_2_out_5, not_5_out);
  PE1 pe1_2 (
    .D3(random_2power_gen_1_out_2), .D2(random_2power_gen_1_out_3), .D1(random_2power_gen_1_out_4),
    .D0(random_2power_gen_1_out_5), .out_5(pe1_2_out_5), .out_6(pe1_2_out_6));
  or or_2 (out_19, and_1_out, and_7_out, and_3_out, and_4_out);
  and and_10 (out_18, pe1_2_out_6, not_5_out);
  not not_1 (not_1_out, random_2power_gen_1_out_2);
  not not_2 (not_2_out, random_2power_gen_1_out_3);
  and and_11 (and_11_out, not_1_out, not_2_out, not_3_out, not_4_out);
  not not_3 (not_3_out, random_2power_gen_1_out_4);
  not not_4 (not_4_out, random_2power_gen_1_out_5);
  not not_5 (not_5_out, and_11_out);
  LED led_17 (.in(not_5_out));
  LED led_18 (.in(and_11_out));

  // Notes on the sheet:
  //   ON INPUT PARKING SYMBOLIZES VACANCY
  //   BUSSES
  //   TRUCKS
  //   4WHEELERS
  //   2WHEELERS
  //   _____________________________
  //   ____________________________
  //   ____________________________
  //   BUSSES
  //   TRUCKS
  //   4WHEELERS
  //   VACANT PARKING SLOT DETECTOR
  //   2WHEELERS
  //   APPROPRIATE VACANT PARKING SLOT DISPLAY (IN BINARY)
  //   SYSTEM ACTIVATE
  //   SYSTEM DEACTIVATE
endmodule

module Random_2Power_Gen (
  input  in_1,
  output out_2,
  output out_3,
  output out_4,
  output out_5
);

  wire not_1_out, not_2_out;
  wire [7:0] random_1_out;

  Random random_1 (.clk(in_1), .out(random_1_out));  // open: next, clr
  not not_1 (not_1_out, random_1_out[0]);
  not not_2 (not_2_out, random_1_out[1]);
  and and_1 (out_2, not_2_out, not_1_out);
  and and_2 (out_3, random_1_out[1], not_1_out);
  and and_3 (out_4, random_1_out[0], not_2_out);
  and and_4 (out_5, random_1_out[0], random_1_out[1]);
endmodule
